# Fritzing sketch schema (saved by Fritzing 0.8.7b)

parts:
  U1 = ESP32-38PinWide [part_number=ESP32-38PinWide]
  Capacitive_Soil_Moisture_Sensor1 = DFRobot Capacitive Soil Moisture Sensor V1.0 [part_number=SEN0193]
  WATER_PUMP1 = water pump/motor
  Q1 = Basic FET N-Channel [package="TO220 [THT]"]
  VCC1 = 4 x AAA Battery Mount
  YF-S201_Flow_Meter1 = YF-S201 Water Flow Meter

nets:
  VCC: U1.3.3, Capacitive_Soil_Moisture_Sensor1.VCC, YF-S201_Flow_Meter1.VCC
  N1: U1.GPIO36, Capacitive_Soil_Moisture_Sensor1.A
  N2: U1.GPIO14, Q1.source
  GND: U1.GND, Capacitive_Soil_Moisture_Sensor1.GND, WATER_PUMP1.pin_1, Q1.gate, Q1.drain, VCC1.-, YF-S201_Flow_Meter1.GND
  N3: U1.GPIO2, YF-S201_Flow_Meter1.SIG
  N4: WATER_PUMP1.pin_2, VCC1.+

custom parts:
  ESP32-38PinWide: Generic 38-Pin ESP32 with wide format (only access to one side of pins on a breadboard) based on Stephen Lilley's HiLetgo ESP-WROOM-32 ESP32 ESP-32S Development Board.
  DFRobot Capacitive Soil Moisture Sensor V1.0: DFRobot Capacitive Soil Moisture Sensor V1.0 This product measures soil moisture levels by capacitive sensing, rather than resistive sensing like other types of moisture sensor. It is made of a corrosion resistant material giving it a long service life. Insert it into soil and impress your friends with the real-time soil moisture data! The product includes an on-board voltage regulator which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
  water pump/motor: WATER PUMP BY ARDUBLOCKTR
  YF-S201 Water Flow Meter: The YF-S201 Flow Meter. The input voltage is 5V to 24V (DC).
